# Fritzing sketch advanced motor (saved by Fritzing 0.9.3b)
breadboards: 1

parts:
  Part1 = Arduino Mega ADK (Rev3)
  IRF520 = Basic FET N-Channel [package="TO220 [THT]"]
  R1 = Resistor [tolerance=±5% resistance=1k package=THT]
  C3 = Electrolytic Capacitor [capacitance=220µF voltage=16V package="200 mil [THT, electrolytic]"]
  D1 = Rectifier Diode [part_number=1N4001 package="300 mil [THT]"]
  M1 = DC Motor
  IC1 = Voltage Regulator [package=to220-igo]
  C8 = Ceramic Capacitor [capacitance=100nF voltage=16V package="200 mil [THT, multilayer]"]
  C9 = Ceramic Capacitor [capacitance=220nF voltage=16V package="200 mil [THT, multilayer]"]

nets:
  GND: Part1.GND, IRF520.source, M1.pin_1, IC1.IN, C8.0, C9.0
  N1: Part1.D2_PWM, R1.Pin_0
  N2: IRF520.gate, R1.Pin_1
  N3: IRF520.drain, C3.-, D1.anode
  N4: C3.+, D1.cathode, M1.pin_2, IC1.OUT, C8.1
  N5: IC1.GND, C9.1

notes:
  N-Channel MOSFET
  IRF520
  current amplification
  +5V
  -V (ground)
  the diode (1N4001 to 1N4007) protects for reverse voltage (coming from the motor....yes, motors can generate electricity :D )
  the electrolytic capacitor (220µF) acts as a filter, removing the "hum" motors make
  if using two or more motors at the same time use a voltage regulator (7805) and a decoupling capacitor circuit for each motor
  LM7805
  100nF
  (=0.1µF)
  [104]
  220nF
  (=0.22µF)
  [224]
