# Fritzing sketch advanced solenoid (saved by Fritzing 0.9.3b)
breadboards: 1

parts:
  Part1 = Arduino Mega ADK (Rev3)
  R1 = Resistor [tolerance=±5% resistance=1k package=THT]
  C3 = Electrolytic Capacitor [capacitance=100µF voltage=25V package="200 mil [THT, electrolytic]"]
  D1 = Rectifier Diode [part_number=1N4001 package="300 mil [THT]"]
  IC1 = Voltage Regulator [package=to220-igo]
  C8 = Ceramic Capacitor [capacitance=100nF voltage=16V package="200 mil [THT, multilayer]"]
  C9 = Ceramic Capacitor [capacitance=220nF voltage=16V package="200 mil [THT, multilayer]"]
  Q1 = TIP120 Hi-Current Darlington Transistor
  L1 = Solenoid

nets:
  GND: Part1.GND, IC1.IN, C8.0, C9.0, Q1.EMITTER
  N1: Part1.D2_PWM, R1.Pin_0
  N2: R1.Pin_1, Q1.BASE
  N3: C3.-, D1.anode, Q1.COLLECTOR, L1.pin2
  N4: C3.+, D1.cathode, IC1.OUT, C8.1, L1.pin1
  N5: IC1.GND, C9.1

notes:
  Darlington Transitor
  current amplification
  +12V
  -V (ground)
  the diode (1N4001 to 1N4007) protects for reverse voltage (coming from the motor....yes, motors can generate electricity :D )
  the electrolytic capacitor (100µF) acts as a filter, removing the "hum" solenoids make
  if using two or more solenoids at the same time use a voltage regulator (7812) and a decoupling capacitor circuit for each motor
  LM7812
  100nF
  (=0.1µF)
  [104]
  220nF
  (=0.22µF)
  [224]
