# Fritzing sketch simple servo (saved by Fritzing 0.9.3b)

parts:
  Part1 = Arduino Mega 2560 (Rev3)
  J1 = Basic Servo

nets:
  5V: Part1.5V, J1.vcc
  N1: Part1.D44, J1.pulse
  GND: Part1.GND, J1.gnd
