# Fritzing sketch simple solenoid (saved by Fritzing 0.9.3b)
breadboards: 1

parts:
  Part1 = Arduino Mega ADK (Rev3)
  R1 = Resistor [tolerance=±5% resistance=1k package=THT]
  C3 = Electrolytic Capacitor [capacitance=100µF voltage=25V package="200 mil [THT, electrolytic]"]
  D1 = Rectifier Diode [part_number=1N4001 package="300 mil [THT]"]
  Q1 = TIP120 Hi-Current Darlington Transistor
  L1 = Solenoid

nets:
  GND: Part1.GND, Q1.EMITTER
  N1: Part1.D2_PWM, R1.Pin_0
  N2: R1.Pin_1, Q1.BASE
  N3: C3.-, D1.anode, Q1.COLLECTOR, L1.pin2
  N4: C3.+, D1.cathode, L1.pin1

notes:
  Darlington Transistor
  TIP120
  current amplification
  +12V
  -V (ground)
  the diode (1N4001 to 1N4007) protects for reverse voltage (coming from the motor....yes, motors can generate electricity :D )
  the electrolytic capacitor (100µF) acts as a filter, removing the "hum" solenoids make
